# Fritzing sketch IRRIGACAO-SMART (saved by Fritzing 0.9.6b)
circuit board: 8.46667cm x 5.64444cm

parts:
  U1 = ESP32-38PinWide [part_number=ESP32-38PinWide]
  HASTE_SOLO = FC-28 Soil Hygrometer Module - Probe
  COMPARADOR_SOLO = FC-28 Soil Hygrometer Module
  S3 = Round Pushbutton
  MODULO_RELE = KY-019 5V Relay Module [package="Breakout board"]
  LED1 = LED - 3mm [color="Red (633nm)" current=0.030 package="3 mm [THT]"]
  LED2 = LED - 3mm [color="Green (570nm)" current=0.030 package="3 mm [THT]"]
  R1 = Resistor [tolerance=±5% resistance=1k package="0805 [SMD]"]
  BOIA = water level switch
  CONECTOR_FEMEA_DC_12V = Power Jack [package=power_jack_slot]
  7805 = Voltage Regulator [package=78xxl]
  BOMBA = DC Motor

nets:
  N1: U1.GPIO34, COMPARADOR_SOLO.AO
  N2: U1.GPIO12, COMPARADOR_SOLO.DO
  GND: U1.GND, COMPARADOR_SOLO.GND, S3.leg0, MODULO_RELE.-, R1.Pin_1, BOIA.pin1, CONECTOR_FEMEA_DC_12V.PWR, CONECTOR_FEMEA_DC_12V.tip_PWR, 7805.GND, BOMBA.pin_1
  N3: U1.GPIO13, MODULO_RELE.S
  VIN: U1.VIN, COMPARADOR_SOLO.VCC, MODULO_RELE.+, 7805.OUT
  N4: U1.GPIO5, BOIA.pin2
  N5: U1.GPIO18, LED1.anode
  N6: U1.GPIO19, LED2.anode
  N7: U1.GPIO23, S3.leg1
  N8: HASTE_SOLO.POS, COMPARADOR_SOLO.POS
  N9: HASTE_SOLO.NEG, COMPARADOR_SOLO.NEG
  N10: MODULO_RELE.Common, CONECTOR_FEMEA_DC_12V.GND, 7805.IN
  N11: MODULO_RELE.NO, BOMBA.pin_2
  N12: LED1.cathode, LED2.cathode, R1.Pin_0

custom parts:
  ESP32-38PinWide: Generic 38-Pin ESP32 with wide format (only access to one side of pins on a breadboard) based on Stephen Lilley's HiLetgo ESP-WROOM-32 ESP32 ESP-32S Development Board.
  FC-28 Soil Hygrometer Module - Probe: The FC-28 is a soil hygrometer module that uses the Texas Instruments LM393 comparator chip to provide an analog measurement of soil humidity.
  FC-28 Soil Hygrometer Module: The FC-28 is a soil hygrometer module that uses the Texas Instruments LM393 comparator chip to provide an analog measurement of soil humidity. The digital output is high when soil moisture is over a certain threshold, as determined by adjusting the potentiometer.
  KY-019 5V Relay Module: KY-019 5V Relay module, used to control AC circuits. (Special thanks to vanepp for fixing the PCB holes and other errors)
  water level switch: Generic water level float switch.
  Power Jack: Power Jack This is the standard 5.5mm barrel jack for power. Ths one is modified to mate with the barrel plug part and allow the two to "connect" so batteries and wall warts can be "connected" in breadboard and will go through to schematic.
